// Logisim project tennis.circ as structural Verilog
module main (
  input  in_1
);

  wire clock_1_out;
  wire [4:0] controller_1_out_3, controller_1_out_4, controller_1_out_5, controller_1_out_6,
       controller_1_out_7, display_1_out_14, display_1_out_15, display_1_out_16, display_1_out_17,
       display_1_out_18, display_2_out_14, display_2_out_15, display_2_out_16, display_2_out_17,
       display_2_out_18, display_3_out_14, display_3_out_15, display_3_out_16, display_3_out_17,
       display_3_out_18;
  wire [31:0] display_1_out_6, display_1_out_7, display_1_out_8, display_1_out_9, display_1_out_10,
       display_1_out_11, display_1_out_12, display_1_out_13, display_2_out_6, display_2_out_7,
       display_2_out_8, display_2_out_9, display_2_out_10, display_2_out_11, display_2_out_12,
       display_2_out_13, display_3_out_6, display_3_out_7, display_3_out_8, display_3_out_9,
       display_3_out_10, display_3_out_11, display_3_out_12, display_3_out_13, display_4_out_6,
       display_4_out_7, display_4_out_8, display_4_out_9, display_4_out_10, display_4_out_11,
       display_4_out_12, display_4_out_13;

  Clock clock_1 (.out(clock_1_out));
  _7_Segment_Display u_7_segment_display_1 ();  // open: g, f, a, b, e, d, c, dp
  DotMatrix #(.matrixcols(32), .matrixrows(32)) dotmatrix_1 (
    .col0(display_1_out_6), .col1(display_1_out_7), .col2(display_1_out_8), .col3(display_1_out_9),
    .col4(display_1_out_10), .col5(display_1_out_11), .col6(display_1_out_12), .col7(display_1_out_13),
    .col8(display_2_out_6), .col9(display_2_out_7), .col10(display_2_out_8), .col11(display_2_out_9),
    .col12(display_2_out_10), .col13(display_2_out_11), .col14(display_2_out_12), .col15(display_2_out_13),
    .col16(display_3_out_6), .col17(display_3_out_7), .col18(display_3_out_8), .col19(display_3_out_9),
    .col20(display_3_out_10), .col21(display_3_out_11), .col22(display_3_out_12), .col23(display_3_out_13),
    .col24(display_4_out_6), .col25(display_4_out_7), .col26(display_4_out_8), .col27(display_4_out_9),
    .col28(display_4_out_10), .col29(display_4_out_11), .col30(display_4_out_12), .col31(display_4_out_13));
  controller controller_1 (
    .in_1(clock_1_out), .in_2(in_1), .out_3(controller_1_out_3), .out_4(controller_1_out_4),
    .out_5(controller_1_out_5), .out_6(controller_1_out_6), .out_7(controller_1_out_7));
  display display_1 (
    .in_1(controller_1_out_3), .in_2(controller_1_out_4), .in_3(controller_1_out_5),
    .in_4(controller_1_out_6), .in_5(controller_1_out_7), .out_14(display_1_out_14),
    .out_15(display_1_out_15), .out_16(display_1_out_16), .out_17(display_1_out_17),
    .out_18(display_1_out_18), .out_8(display_1_out_8), .out_6(display_1_out_6), .out_7(display_1_out_7),
    .out_9(display_1_out_9), .out_10(display_1_out_10), .out_11(display_1_out_11), .out_12(display_1_out_12),
    .out_13(display_1_out_13));
  display display_2 (
    .in_1(display_1_out_14), .in_2(display_1_out_15), .in_3(display_1_out_16), .in_4(display_1_out_17),
    .in_5(display_1_out_18), .out_14(display_2_out_14), .out_15(display_2_out_15), .out_16(display_2_out_16),
    .out_17(display_2_out_17), .out_18(display_2_out_18), .out_8(display_2_out_8), .out_6(display_2_out_6),
    .out_7(display_2_out_7), .out_9(display_2_out_9), .out_10(display_2_out_10), .out_11(display_2_out_11),
    .out_12(display_2_out_12), .out_13(display_2_out_13));
  display display_3 (
    .in_1(display_2_out_14), .in_2(display_2_out_15), .in_3(display_2_out_16), .in_4(display_2_out_17),
    .in_5(display_2_out_18), .out_14(display_3_out_14), .out_15(display_3_out_15), .out_16(display_3_out_16),
    .out_17(display_3_out_17), .out_18(display_3_out_18), .out_8(display_3_out_8), .out_6(display_3_out_6),
    .out_7(display_3_out_7), .out_9(display_3_out_9), .out_10(display_3_out_10), .out_11(display_3_out_11),
    .out_12(display_3_out_12), .out_13(display_3_out_13));
  _7_Segment_Display u_7_segment_display_2 ();  // open: g, f, a, b, e, d, c, dp
  display display_4 (
    .in_1(display_3_out_14), .in_2(display_3_out_15), .in_3(display_3_out_16), .in_4(display_3_out_17),
    .in_5(display_3_out_18), .out_8(display_4_out_8), .out_6(display_4_out_6), .out_7(display_4_out_7),
    .out_9(display_4_out_9), .out_10(display_4_out_10), .out_11(display_4_out_11), .out_12(display_4_out_12),
    .out_13(display_4_out_13));  // open: out_14, out_15, out_16, out_17, out_18
endmodule

module inc (
  input  [4:0] in_1,
  output [4:0] out_2
);

  Adder #(.width(5)) adder_1 (.a(in_1), .b(5'b00001), .out(out_2));  // open: cin, cout
endmodule

module display (
  input  [4:0] in_1,
  input  [4:0] in_2,
  input  [4:0] in_3,
  input  [4:0] in_4,
  input  [4:0] in_5,
  output [31:0] out_6,
  output [31:0] out_7,
  output [31:0] out_8,
  output [31:0] out_9,
  output [31:0] out_10,
  output [31:0] out_11,
  output [31:0] out_12,
  output [31:0] out_13,
  output [4:0] out_14,
  output [4:0] out_15,
  output [4:0] out_16,
  output [4:0] out_17,
  output [4:0] out_18
);

  wire _0, _1, _2, _3, _4, _5, _6, _7, comparator_1_eq, comparator_2_eq, comparator_3_eq;
  wire [4:0] divider_1_out, divider_1_rem;
  wire [31:0] l_bat32, multiplexer_1_out, multiplexer_2_out, multiplexer_3_out, multiplexer_4_out,
       multiplexer_5_out, multiplexer_6_out, multiplexer_7_out, multiplexer_8_out, pull_resistor_4_node,
       pull_resistor_7_node, r_bat32, y32;

  assign out_6 = {32{1'b0}} | multiplexer_1_out;  // OR_Gate or_1, 32 bits wide
  Multiplexer #(.width(32)) multiplexer_1 (.in0({32{1'b0}}), .in1(y32), .out(multiplexer_1_out), .sel(_0));  // open: en
  Pull_Resistor pull_resistor_1 (.node(_0));
  Pull_Resistor pull_resistor_2 (.node(_1));
  assign out_7 = {32{1'b0}} | multiplexer_2_out;  // OR_Gate or_2, 32 bits wide
  Multiplexer #(.width(32)) multiplexer_2 (.in0({32{1'b0}}), .in1(y32), .out(multiplexer_2_out), .sel(_1));  // open: en
  Comparator #(.width(5), .mode("unsigned")) comparator_1 (
    .a(in_1), .b({5{1'b0}}), .eq(comparator_1_eq));  // open: gt, lt
  assign out_8 = {32{1'b0}} | multiplexer_3_out;  // OR_Gate or_3, 32 bits wide
  Multiplexer #(.width(32)) multiplexer_3 (.in0({32{1'b0}}), .in1(y32), .out(multiplexer_3_out), .sel(_2));  // open: en
  Pull_Resistor pull_resistor_3 (.node(_2));
  Pull_Resistor pull_resistor_4 (.node(pull_resistor_4_node));
  assign pull_resistor_4_node = comparator_1_eq ? l_bat32 : 32'bz;  // Controlled_Buffer controlled_buffer_1
  assign out_9 = {32{1'b0}} | pull_resistor_4_node | multiplexer_4_out;  // OR_Gate or_4, 32 bits wide
  Multiplexer #(.width(32)) multiplexer_4 (.in0({32{1'b0}}), .in1(y32), .out(multiplexer_4_out), .sel(_3));  // open: en
  Pull_Resistor pull_resistor_5 (.node(_3));
  Comparator #(.width(5), .mode("unsigned")) comparator_2 (
    .a(in_1), .b(5'b00011), .eq(comparator_2_eq));  // open: gt, lt
  inc inc_1 (.in_1(in_1), .out_2(out_14));
  assign out_10 = {32{1'b0}} | pull_resistor_7_node | multiplexer_5_out;  // OR_Gate or_5, 32 bits wide
  Pull_Resistor pull_resistor_6 (.node(_4));
  Pull_Resistor pull_resistor_7 (.node(pull_resistor_7_node));
  assign pull_resistor_7_node = comparator_2_eq ? r_bat32 : 32'bz;  // Controlled_Buffer controlled_buffer_2
  Multiplexer #(.width(32)) multiplexer_5 (.in0({32{1'b0}}), .in1(y32), .out(multiplexer_5_out), .sel(_4));  // open: en
  assign out_11 = {32{1'b0}} | multiplexer_6_out;  // OR_Gate or_6, 32 bits wide
  Pull_Resistor pull_resistor_8 (.node(_5));
  Comparator #(.width(5)) comparator_3 (.a(in_1), .b(divider_1_out), .eq(comparator_3_eq));  // open: gt, lt
  Divider #(.width(5)) divider_1 (.a(in_2), .b(5'b01000), .out(divider_1_out), .rem(divider_1_rem));  // open: upper
  Multiplexer #(.width(32)) multiplexer_6 (.in0({32{1'b0}}), .in1(y32), .out(multiplexer_6_out), .sel(_5));  // open: en
  Shifter #(.width(32)) shifter_1 (.in(32'h1), .\dist (in_3), .out(y32));
  Shifter #(.width(32)) shifter_2 (.in(32'h7), .\dist (in_4), .out(l_bat32));
  Shifter #(.width(32)) shifter_3 (.in(32'h7), .\dist (in_5), .out(r_bat32));
  assign out_12 = {32{1'b0}} | multiplexer_7_out;  // OR_Gate or_7, 32 bits wide
  Pull_Resistor pull_resistor_9 (.node(_6));
  Decoder #(.select(3)) decoder_1 (
    .out0(_0), .out1(_1), .out2(_2), .out3(_3), .out4(_4), .out5(_5), .out6(_6), .out7(_7),
    .sel(divider_1_rem[2:0]), .en(comparator_3_eq));
  Multiplexer #(.width(32)) multiplexer_7 (.in0({32{1'b0}}), .in1(y32), .out(multiplexer_7_out), .sel(_6));  // open: en
  assign out_13 = {32{1'b0}} | multiplexer_8_out;  // OR_Gate or_8, 32 bits wide
  Multiplexer #(.width(32)) multiplexer_8 (.in0({32{1'b0}}), .in1(y32), .out(multiplexer_8_out), .sel(_7));  // open: en
  Pull_Resistor pull_resistor_10 (.node(_7));

  assign out_15 = in_2;
  assign out_16 = in_3;
  assign out_17 = in_4;
  assign out_18 = in_5;

  // Other names for the same wires on the sheet: l_bat[4:0] = in_4; r_bat[4:0] = in_5; y[4:0] = in_3
endmodule

module controller (
  input  in_1,
  input  in_2,
  output [4:0] out_3,
  output [4:0] out_4,
  output [4:0] out_5,
  output [4:0] out_6,
  output [4:0] out_7
);

  wire [2:0] motion_1_new_cords, motion_1_new_speed, motion_2_new_cords, motion_2_new_speed,
       multiplexer_1_out, multiplexer_2_out, vx_q, vy_q;
  wire [7:0] multiplexer_3_out, multiplexer_4_out, x_q, y_q;

  Register #(.width(3)) speed (.clk(in_1));  // open: D, en, Q, clr
  Multiplexer #(.width(3)) multiplexer_1 (
    .in0(motion_1_new_speed), .in1(3'b001), .out(multiplexer_1_out), .sel(in_2));  // open: en
  Multiplexer #(.width(3)) multiplexer_2 (
    .in0(motion_2_new_speed), .in1(3'b001), .out(multiplexer_2_out), .sel(in_2));  // open: en
  Register #(.width(3)) vy (.D(multiplexer_2_out), .Q(vy_q), .clk(in_1));  // open: en, clr
  Multiplexer #(.width(8)) multiplexer_3 (
    .in0({out_4, motion_1_new_cords}), .in1(8'h10), .out(multiplexer_3_out), .sel(in_2));  // open: en
  Register #(.width(3)) vx (.D(multiplexer_1_out), .Q(vx_q), .clk(in_1));  // open: en, clr
  Multiplexer #(.width(8)) multiplexer_4 (
    .in0({out_5, motion_2_new_cords}), .in1(8'h50), .out(multiplexer_4_out), .sel(in_2));  // open: en
  Register x (.D(multiplexer_3_out), .Q(x_q), .clk(in_1));  // open: en, clr
  motion motion_1 (.in_1(x_q), .speed(vx_q), .new_cords({out_4, motion_1_new_cords}), .new_speed(motion_1_new_speed));
  Register y (.D(multiplexer_4_out), .Q(y_q), .clk(in_1));  // open: en, clr
  motion motion_2 (.in_1(y_q), .speed(vy_q), .new_cords({out_5, motion_2_new_cords}), .new_speed(motion_2_new_speed));

  assign out_3 = {5{1'b0}};
  assign out_6 = {5{1'b0}};
  assign out_7 = {5{1'b0}};

  // Other names for the same wires on the sheet: clock = in_1; reset = in_2
endmodule

module reflect (
  input  [2:0] speed,
  input  cout,
  output [2:0] out_3,
  output out_4
);

  wire [2:0] negator_1_out;

  Negator #(.width(3)) negator_1 (.in(speed), .out(negator_1_out));
  xor xor_1 (out_4, speed[2], cout);
  Multiplexer #(.width(3)) multiplexer_1 (.in0(speed), .in1(negator_1_out), .out(out_3), .sel(out_4));  // open: en
endmodule

module motion (
  input  [7:0] in_1,
  input  [2:0] speed,
  output [7:0] new_cords,
  output [2:0] new_speed
);

  wire adder_1_cout, reflect_1_out_4;
  wire [7:0] adder_1_out, bit_extender_1_out;

  assign bit_extender_1_out = {{5{speed[2]}}, speed};  // Bit_Extender bit_extender_1
  Adder adder_1 (.a(in_1), .b(bit_extender_1_out), .out(adder_1_out), .cout(adder_1_cout));  // open: cin
  reflect reflect_1 (.speed(speed), .cout(adder_1_cout), .out_3(new_speed), .out_4(reflect_1_out_4));
  Multiplexer #(.width(8)) multiplexer_1 (
    .in0(adder_1_out), .in1(in_1), .out(new_cords), .sel(reflect_1_out_4));  // open: en
endmodule
